// Logisim project ALU.circ as structural Verilog: 1 circuit, main circuit ALU
module ALU (
  input  [5:0] ALUOpExt,
  input  isShift,
  input  [15:0] Op0,
  input  [15:0] Op1,
  input  shiftType,
  output A_eq_B,
  output [15:0] ALUOut,
  output Cout,
  output Overflow
);

  wire and_1_out, nor_1_out, nor_2_out, nor_3_out, nor_4_out, sn74ls181_1_p11, sn74ls181_2_p11,
       sn74ls181_3_p11, xor_1_out;
  wire [15:0] multiplexer_1_out, shifter_1_out, shifter_2_out, sn74ls181_1_p5;

  Shifter #(.width(16)) shifter_1 (.in(Op0), .\dist (Op1[3:0]), .out(shifter_1_out));
  Shifter #(.shift("lr"), .width(16)) shifter_2 (.in(Op0), .\dist (Op1[3:0]), .out(shifter_2_out));
  // sn74ls181 sn74ls181_1: pin names not known; wires that end beside it: ALUOpExt[1], ALUOpExt[0], ALUOpExt[5], ALUOpExt[4], sn74ls181_1_p5[0], sn74ls181_1_p5[1], sn74ls181_1_p5[2], Op1[2], Op0[3], Op1[3], sn74ls181_1_p11, sn74ls181_1_p5[3]
  // sn74ls181 sn74ls181_2: pin names not known; wires that end beside it: ALUOpExt[1], ALUOpExt[0], sn74ls181_1_p11, ALUOpExt[4], sn74ls181_1_p5[4], sn74ls181_1_p5[5], sn74ls181_1_p5[6], Op1[6], Op0[7], Op1[7], sn74ls181_2_p11, sn74ls181_1_p5[7]
  // sn74ls181 sn74ls181_3: pin names not known; wires that end beside it: ALUOpExt[1], ALUOpExt[0], sn74ls181_2_p11, ALUOpExt[4], sn74ls181_1_p5[8], sn74ls181_1_p5[9], sn74ls181_1_p5[10], Op1[10], Op0[11], Op1[11], sn74ls181_3_p11, sn74ls181_1_p5[11]
  // sn74ls181 sn74ls181_4: pin names not known; wires that end beside it: ALUOpExt[1], ALUOpExt[0], sn74ls181_3_p11, ALUOpExt[4], sn74ls181_1_p5[12], sn74ls181_1_p5[13], sn74ls181_1_p5[14], Op1[14], Op0[15], Op1[15], Cout, sn74ls181_1_p5[15]
  and and_1 (and_1_out, Op0[15], Op1[15]);
  Multiplexer #(.width(16)) multiplexer_1 (
    .in0(shifter_1_out), .in1(shifter_2_out), .out(multiplexer_1_out), .sel(shiftType));
  nor nor_1 (nor_1_out, sn74ls181_1_p5[0], sn74ls181_1_p5[1], sn74ls181_1_p5[2], sn74ls181_1_p5[3]);
  nor nor_2 (nor_2_out, sn74ls181_1_p5[6], sn74ls181_1_p5[5], sn74ls181_1_p5[4], sn74ls181_1_p5[7]);
  nor nor_3 (nor_3_out, sn74ls181_1_p5[10], sn74ls181_1_p5[9], sn74ls181_1_p5[8], sn74ls181_1_p5[11]);
  nor nor_4 (nor_4_out, sn74ls181_1_p5[12], sn74ls181_1_p5[13], sn74ls181_1_p5[14], sn74ls181_1_p5[15]);
  xor xor_1 (xor_1_out, sn74ls181_1_p5[15], and_1_out);
  and and_2 (Overflow, ALUOpExt[5], xor_1_out);
  and and_3 (A_eq_B, nor_1_out, nor_2_out, nor_3_out, nor_4_out);
  Multiplexer #(.width(16)) multiplexer_2 (.in0(sn74ls181_1_p5), .in1(multiplexer_1_out), .out(ALUOut), .sel(isShift));

  // Notes on the sheet:
  //   MSB di B
  //   0
  //   1
  //   bits 0 to 3 are ALUOp, bit 4 is Mode, bit 5 is Cin
  //   MSB di A
  //   0
  //   1
  //   if MSB_A=MSB_B=!MSB_R then Overflow = 1
  //   OVERFLOW DETECTOR
  //   MSB del ris
  //   1
  //   0
  //   Only when performing addition (Cin = 1)
endmodule
