// Logisim project data_memory.circ as structural Verilog: 1 circuit, main circuit data_memory
module data_memory (
  input  CLK,
  input  WE,
  input  [15:0] WriteData,
  input  [15:0] Address
);

  wire n74273_1_pin11, n74283_1_pin2, n74283_1_pin7, n74283_2_pin7, n74283_3_pin7, n74283_4_pin7;
  wire [7:0] demultiplexer_1_out0, demultiplexer_1_out1, multiplexer_1_out, n74273_1_pin2, n74273_2_pin2,
       n74273_3_pin2, n74273_4_pin2, ram_1_dout;
  wire [15:0] n74283_4_pin4;

  _74273 u_74273_1 (
    .pin2(n74273_1_pin2[0]), .pin3(WriteData[0]), .pin4(WriteData[1]), .pin5(n74273_1_pin2[1]),
    .pin6(n74273_1_pin2[2]), .pin7(WriteData[2]), .pin8(WriteData[3]), .pin9(n74273_1_pin2[3]),
    .pin19(n74273_1_pin2[7]), .pin18(WriteData[7]), .pin17(WriteData[6]), .pin16(n74273_1_pin2[6]),
    .pin15(n74273_1_pin2[5]), .pin14(WriteData[5]), .pin13(WriteData[4]), .pin12(n74273_1_pin2[4]),
    .pin11(n74273_1_pin11));  // open: pin1
  _74273 u_74273_2 (
    .pin2(n74273_2_pin2[0]), .pin3(WriteData[8]), .pin4(WriteData[9]), .pin5(n74273_2_pin2[1]),
    .pin6(n74273_2_pin2[2]), .pin7(WriteData[10]), .pin8(WriteData[11]), .pin9(n74273_2_pin2[3]),
    .pin19(n74273_2_pin2[7]), .pin18(WriteData[15]), .pin17(WriteData[14]), .pin16(n74273_2_pin2[6]),
    .pin15(n74273_2_pin2[5]), .pin14(WriteData[13]), .pin13(WriteData[12]), .pin12(n74273_2_pin2[4]));  // open: pin1, pin11
  Multiplexer #(.width(8)) multiplexer_1 (.in0(n74273_2_pin2), .in1(n74273_1_pin2), .out(multiplexer_1_out), .sel(CLK));
  _74283 u_74283_1 (
    .pin1(n74283_4_pin4[13]), .pin2(n74283_1_pin2), .pin3(Address[13]), .pin4(n74283_4_pin4[12]),
    .pin5(Address[12]), .pin6(n74283_1_pin2), .pin7(n74283_1_pin7), .pin15(n74283_1_pin2),
    .pin14(Address[14]), .pin13(n74283_4_pin4[14]), .pin12(Address[15]), .pin11(n74283_1_pin2),
    .pin10(n74283_4_pin4[15]));  // open: pin9
  _74283 u_74283_2 (
    .pin1(n74283_4_pin4[9]), .pin2(n74283_1_pin2), .pin3(Address[9]), .pin4(n74283_4_pin4[8]),
    .pin5(Address[8]), .pin6(n74283_1_pin2), .pin7(n74283_2_pin7), .pin15(n74283_1_pin2),
    .pin14(Address[10]), .pin13(n74283_4_pin4[10]), .pin12(Address[11]), .pin11(n74283_1_pin2),
    .pin10(n74283_4_pin4[11]), .pin9(n74283_1_pin7));
  RAM #(.addrWidth(16)) ram_1 (
    .addr(n74283_4_pin4), .we(WE), .oe(1'b1), .clk(CLK), .din(multiplexer_1_out), .dout(ram_1_dout));
  _74283 u_74283_3 (
    .pin1(n74283_4_pin4[5]), .pin2(n74283_1_pin2), .pin3(Address[5]), .pin4(n74283_4_pin4[4]),
    .pin5(Address[4]), .pin6(n74283_1_pin2), .pin7(n74283_3_pin7), .pin15(n74283_1_pin2), .pin14(Address[6]),
    .pin13(n74283_4_pin4[6]), .pin12(Address[7]), .pin11(n74283_1_pin2), .pin10(n74283_4_pin4[7]),
    .pin9(n74283_2_pin7));
  _74283 u_74283_4 (
    .pin1(n74283_4_pin4[1]), .pin2(n74283_1_pin2), .pin3(Address[1]), .pin4(n74283_4_pin4[0]),
    .pin5(Address[0]), .pin6(n74283_1_pin2), .pin7(n74283_4_pin7), .pin15(n74283_1_pin2), .pin14(Address[2]),
    .pin13(n74283_4_pin4[2]), .pin12(Address[3]), .pin11(n74283_1_pin2), .pin10(n74283_4_pin4[3]),
    .pin9(n74283_3_pin7));
  Demultiplexer #(.width(8)) demultiplexer_1 (
    .out0(demultiplexer_1_out0), .out1(demultiplexer_1_out1), .in(ram_1_dout), .sel(CLK));
  not not_1 (n74283_4_pin7, CLK);
  _74273 u_74273_3 (
    .pin2(n74273_3_pin2[0]), .pin3(demultiplexer_1_out1[0]), .pin4(demultiplexer_1_out1[1]),
    .pin5(n74273_3_pin2[1]), .pin6(n74273_3_pin2[2]), .pin7(demultiplexer_1_out1[2]),
    .pin8(demultiplexer_1_out1[3]), .pin9(n74273_3_pin2[3]), .pin19(n74273_3_pin2[7]),
    .pin18(demultiplexer_1_out1[7]), .pin17(demultiplexer_1_out1[6]), .pin16(n74273_3_pin2[6]),
    .pin15(n74273_3_pin2[5]), .pin14(demultiplexer_1_out1[5]), .pin13(demultiplexer_1_out1[4]),
    .pin12(n74273_3_pin2[4]));  // open: pin1, pin11
  _74273 u_74273_4 (
    .pin2(n74273_4_pin2[0]), .pin3(demultiplexer_1_out0[0]), .pin4(demultiplexer_1_out0[1]),
    .pin5(n74273_4_pin2[1]), .pin6(n74273_4_pin2[2]), .pin7(demultiplexer_1_out0[2]),
    .pin8(demultiplexer_1_out0[3]), .pin9(n74273_4_pin2[3]), .pin19(n74273_4_pin2[7]),
    .pin18(demultiplexer_1_out0[7]), .pin17(demultiplexer_1_out0[6]), .pin16(n74273_4_pin2[6]),
    .pin15(n74273_4_pin2[5]), .pin14(demultiplexer_1_out0[5]), .pin13(demultiplexer_1_out0[4]),
    .pin12(n74273_4_pin2[4]));  // open: pin1, pin11
  // also tied to GND on the sheet: n74283_1_pin2

  // Notes on the sheet:
  //   since it's little endiand, first is written lower byte
  //   this brought me to map lower byte to "1" mux port
  //   so when clock is high, the first byte is selected
  //   When clock turns low, the second byte is selected
  //   Same logic can be applied to the output data
  //   I HAVE TO ADD A CONDITION TO WRITE TO THE REGISTER
  //   I WRITE TO IT ONLY IF REGISTER IS SELECTED
endmodule
