// Logisim project flags.circ as structural Verilog: 1 circuit, main circuit flags
module flags (
  input  CLK,
  input  FlagWrite,
  input  [3:0] FlagsIN,
  output [3:0] FlagOut
);

  wire n74175_1_pin9;

  _74175 u_74175_1 (
    .pin2(FlagOut[0]), .pin4(FlagsIN[0]), .pin5(FlagsIN[1]), .pin7(FlagOut[1]), .pin15(FlagOut[3]),
    .pin13(FlagsIN[3]), .pin12(FlagsIN[2]), .pin10(FlagOut[2]), .pin9(n74175_1_pin9));  // open: pin1, pin3, pin6, pin14, pin11
  and and_1 (n74175_1_pin9, CLK, FlagWrite);
endmodule
