// Logisim project instruction_RAM.circ as structural Verilog: 1 circuit, main circuit instruction_RAM
module instruction_RAM (
  input  CLK,
  input  [15:0] InstrAddr,
  input  WE,
  input  [15:0] InstrIN,
  output [15:0] Instruction
);

  RAM #(.addrWidth(16)) ram_1 (
    .addr(InstrAddr), .we(WE), .oe(1'b1), .clk(CLK), .din(InstrIN[7:0]), .dout(Instruction[7:0]));
  RAM #(.addrWidth(16)) ram_2 (
    .addr(InstrAddr), .we(WE), .oe(1'b1), .clk(CLK), .din(InstrIN[15:8]), .dout(Instruction[15:8]));
endmodule
