// Logisim project program_counter.circ as structural Verilog: 1 circuit, main circuit program_counter
module program_counter (
  input  CLK,
  input  WE,
  input  isJumping,
  input  [15:0] AddrImm,
  input  [15:0] AddrReg,
  input  JumpSrc,
  input  isInit,
  input  [15:0] InitValue,
  output [15:0] InstrAddr
);

  wire A_out, and_1_out, and_2_out, and_3_out, not_1_out, not_2_out, not_3_out, or_1_out;
  wire [15:0] adder_1_out, multiplexer_1_out, multiplexer_2_out, multiplexer_3_out;

  Multiplexer #(.width(16)) multiplexer_1 (.in0({16{1'b0}}), .in1(AddrImm), .out(multiplexer_1_out), .sel(isJumping));
  not not_1 (not_1_out, isJumping);
  Multiplexer #(.width(16)) multiplexer_2 (.in0(InitValue), .in1(AddrReg), .out(multiplexer_2_out), .sel(A_out));
  and A (A_out, and_2_out, not_3_out);
  not not_2 (not_2_out, and_3_out);
  and and_1 (and_1_out, not_1_out, not_2_out);
  Adder #(.width(16)) adder_1 (.a(InstrAddr), .b(multiplexer_1_out), .out(adder_1_out), .cin(and_1_out));  // open: cout
  not not_3 (not_3_out, isInit);
  and and_2 (and_2_out, isJumping, JumpSrc);
  Multiplexer #(.width(16)) multiplexer_3 (
    .in0(adder_1_out), .in1(multiplexer_2_out), .out(multiplexer_3_out), .sel(or_1_out));
  or or_1 (or_1_out, and_2_out, isInit);
  and and_3 (and_3_out, CLK, WE);
  _74273 u_74273_1 (
    .pin2(InstrAddr[0]), .pin3(multiplexer_3_out[0]), .pin4(multiplexer_3_out[1]), .pin5(InstrAddr[1]),
    .pin6(InstrAddr[2]), .pin7(multiplexer_3_out[2]), .pin8(multiplexer_3_out[3]), .pin9(InstrAddr[3]),
    .pin19(InstrAddr[7]), .pin18(multiplexer_3_out[7]), .pin17(multiplexer_3_out[6]), .pin16(InstrAddr[6]),
    .pin15(InstrAddr[5]), .pin14(multiplexer_3_out[5]), .pin13(multiplexer_3_out[4]), .pin12(InstrAddr[4]),
    .pin11(and_3_out));  // open: pin1
  _74273 u_74273_2 (
    .pin2(InstrAddr[8]), .pin3(multiplexer_3_out[8]), .pin4(multiplexer_3_out[9]), .pin5(InstrAddr[9]),
    .pin6(InstrAddr[10]), .pin7(multiplexer_3_out[10]), .pin8(multiplexer_3_out[11]), .pin9(InstrAddr[11]),
    .pin19(InstrAddr[15]), .pin18(multiplexer_3_out[15]), .pin17(multiplexer_3_out[14]),
    .pin16(InstrAddr[14]), .pin15(InstrAddr[13]), .pin14(multiplexer_3_out[13]),
    .pin13(multiplexer_3_out[12]), .pin12(InstrAddr[12]), .pin11(and_3_out));  // open: pin1

  // Notes on the sheet:
  //   when jump address is contained in 
  //   a register, it's NOT an offset, so it's must be directly
  //   loaded into PC and not added to PC
  //   For example, when returning from a function call,
  //   ra must be loaded into PC
  //   and gate (A) needed because if 
  //   isInit = 1, JumpSrc must not influence
  //   the init process
endmodule
