// Logisim project cpu_circuit.circ as structural Verilog: 2 circuits, main circuit main
module main (
  input  isInit
);

  wire alu_1_p3, and_1_out, clock_1_out, control_unit_1_p2, instruction_decoder_1_type_size,
       mask_checker_1_equal, or_1_out, undriven, undriven_2, undriven_3, undriven_4, undriven_5, undriven_7,
       undriven_8, undriven_9, undriven_10, undriven_11;
  wire [1:0] control_unit_1_p1, undriven_6;
  wire [2:0] flags_1_flagout, instruction_decoder_1_mask;
  wire [3:0] alu_1_p4, instruction_decoder_1_rd, instruction_decoder_1_rs, multiplexer_1_out;
  wire [3:3] flags_1_flagout_2;
  wire [4:0] instruction_decoder_1_opcode;
  wire [9:0] instruction_decoder_1_immediate;
  wire [15:0] alu_1_p5, bit_extender_1_out, bit_extender_2_out, bit_extender_3_out, data_memory_1_readdata,
       instruction_ram_1_instruction, multiplexer_2_out, multiplexer_3_out, multiplexer_4_out,
       multiplexer_5_out, multiplexer_6_out, multiplexer_7_out, program_counter_1_instraddr,
       register_file_1_readdata0, register_file_1_readdata1;

  program_counter program_counter_1 (
    .CLK(clock_1_out), .WE(clock_1_out), .isJumping(or_1_out), .AddrImm(multiplexer_2_out),
    .AddrReg(register_file_1_readdata0), .InitValue({16{1'b0}}), .JumpSrc(undriven), .isInit(isInit),
    .InstrAddr(program_counter_1_instraddr));
  or or_1 (or_1_out, and_1_out, undriven_2);
  and and_1 (and_1_out, mask_checker_1_equal, undriven_3);
  Clock clock_1 (.out(clock_1_out));
  mask_checker mask_checker_1 (
    .mask(instruction_decoder_1_mask), .flags(flags_1_flagout), .equal(mask_checker_1_equal));
  instruction_RAM instruction_ram_1 (
    .InstrIN({16{1'b0}}), .InstrAddr(program_counter_1_instraddr), .WE(1'b0), .CLK(clock_1_out),
    .Instruction(instruction_ram_1_instruction));
  instruction_decoder instruction_decoder_1 (
    .Instruction(instruction_ram_1_instruction), .OpCode(instruction_decoder_1_opcode),
    .Mask(instruction_decoder_1_mask), .rd(instruction_decoder_1_rd), .rs(instruction_decoder_1_rs),
    .Type_Size(instruction_decoder_1_type_size), .Immediate(instruction_decoder_1_immediate));
  Multiplexer #(.select(2), .width(4)) multiplexer_1 (
    .in0(instruction_decoder_1_rd), .in1(4'b0011), .in2(4'b0010), .out(multiplexer_1_out),
    .sel(control_unit_1_p1));  // open: in3
  assign bit_extender_1_out = {{6{instruction_decoder_1_immediate[9]}}, instruction_decoder_1_immediate};  // Bit_Extender bit_extender_1
  assign bit_extender_2_out = {{8{instruction_decoder_1_immediate[9]}}, instruction_decoder_1_immediate[9:2]};  // Bit_Extender bit_extender_2
  assign bit_extender_3_out = {{10{instruction_decoder_1_immediate[9]}}, instruction_decoder_1_immediate[9:4]};  // Bit_Extender bit_extender_3
  flags flags_1 (
    .FlagsIN(alu_1_p4), .CLK(clock_1_out), .FlagWrite(undriven_4),
    .FlagOut({flags_1_flagout_2[3], flags_1_flagout}));
  Multiplexer #(.select(2), .width(16)) multiplexer_2 (
    .in0(bit_extender_1_out), .in1(bit_extender_2_out), .in2(bit_extender_3_out), .out(multiplexer_2_out),
    .sel(undriven_6));  // open: in3
  // control_unit control_unit_1: pin names not known; wires that end beside it: control_unit_1_p1[0], control_unit_1_p2
  register_file register_file_1 (
    .CLK(clock_1_out), .RegWrite(undriven_5), .ReadAddr0(instruction_decoder_1_rd),
    .ReadAddr1(instruction_decoder_1_rs), .WriteData(multiplexer_7_out), .WriteAddr(multiplexer_1_out),
    .ReadData0(register_file_1_readdata0), .ReadData1(register_file_1_readdata1));
  Multiplexer #(.width(16)) multiplexer_3 (
    .in0(register_file_1_readdata0), .in1(program_counter_1_instraddr), .out(multiplexer_3_out),
    .sel(undriven_7));
  Multiplexer #(.width(16)) multiplexer_4 (
    .in0(register_file_1_readdata1), .in1(multiplexer_2_out), .out(multiplexer_4_out), .sel(undriven_8));
  // ALU alu_1: pin names not known; wires that end beside it: multiplexer_4_out, control_unit_1_p2, alu_1_p3, alu_1_p4, alu_1_p5
  Multiplexer #(.width(16)) multiplexer_5 (
    .in0(register_file_1_readdata1), .in1(register_file_1_readdata0), .out(multiplexer_5_out),
    .sel(undriven_9));
  Multiplexer #(.width(16)) multiplexer_6 (
    .in0(register_file_1_readdata1), .in1({16{1'b0}}), .out(multiplexer_6_out), .sel(isInit));
  data_memory data_memory_1 (
    .MemWrite(undriven_9), .CLK(clock_1_out), .MemRead(undriven_10), .WriteData(multiplexer_6_out),
    .Address(multiplexer_5_out), .Size(instruction_decoder_1_type_size), .ReadData(data_memory_1_readdata));
  Multiplexer #(.width(16)) multiplexer_7 (
    .in0(alu_1_p5), .in1(data_memory_1_readdata), .out(multiplexer_7_out), .sel(undriven_11));

  // Notes on the sheet:
  //   should WE = CLK for real?
  //   in this circuit there must not be input pins
  //   A Clock module should be better
  //   currently not using 4th flags bit
  //   rd
  //   ra=t3
  //   lui_rd=t2
  //   00 = rd
  //   01 = ra
  //   10 = lui_rd
  //   missing RF input "T/S"
  //   InitData
endmodule

module mask_checker (
  input  [2:0] mask,
  input  [2:0] flags,
  output equal
);

  Comparator #(.width(3)) comparator_1 (.a(mask), .b(flags), .eq(equal));  // open: gt, lt
endmodule
